# Fritzing sketch capteur_wifi_plante (saved by Fritzing 0.9.2b)
circuit board: 5.51911cm x 2.06883cm
breadboards: 1

parts:
  Composant1 = Arduino Nano (Rev3.0)
  Espessif_Serial_Wifi_Modul_1 = ESP8266 ESP01 [part_number=ESP8266 package=THT]

nets:
  GND: Composant1.GND, Espessif_Serial_Wifi_Modul_1.GND
  N1: Composant1.D10, Espessif_Serial_Wifi_Modul_1.TXD
  N2: Composant1.D11/MOSI, Espessif_Serial_Wifi_Modul_1.RXD
  3V3: Composant1.3V3, Espessif_Serial_Wifi_Modul_1.VCC, Espessif_Serial_Wifi_Modul_1.CH_PD

custom parts:
  ESP8266 ESP01: Generic WiFi Module based on the ESP8266 with onboard PCB antenna and UART communications
